# Fritzing sketch Costco_controller (saved by Fritzing 0.9.3b)

parts:
  U1 = Voltage Regulator [part_number=78M05 package=to220-igo]
  LED_Strip1 = Molex Picoblade Series Header [package=Picoblade-53398-0571]
  Power_plug1 = Power plug
  Q2 = Basic FET N-Channel [part_number=VS3019AD package="TO220 [THT]"]
  Q1 = Basic FET N-Channel [part_number=CMD20P03 package="TO220 [THT]"]
  L5 = Ceramic Capacitor [capacitance="100 nF" package="0805 [SMD, multilayer]"]
  IC4 = IC, DIP package, 20 pins [chip_label=IC part_number=STM8S003F3]
  R1 = Resistor [tolerance=±5% resistance=220 package=THT]
  IR1 = TSOP312.., 314.. [package=THT]
  C2 = Electrolytic Capacitor [capacitance=1mF voltage=35V package="100 mil [THT, electrolytic]"]

nets:
  GND: U1.GND, Power_plug1.GND, C2.-
  N1: U1.IN, LED_Strip1.1, Power_plug1.VCC, C2.+
  N2: LED_Strip1.2, R1.Pin_1
  N3: LED_Strip1.4, Q2.drain
  N4: LED_Strip1.5, L5.1
  N5: Q1.drain, L5.0
  N6: IC4.pin1, R1.Pin_0
  N7: IC4.pin10, IR1.Data

notes:
  Costco Controller, ESP8266/RGB+W/WS2812 LED Strip controller, 2.0
  LED Strip Connector
  1 - 24V - Black
  2 - DIN - Red
  3 - Check - Green
  4 - W - Yellow
  5 - Gnd - Blue
