# Fritzing sketch mculed_v3_strip (saved by Fritzing 0.9.3b)
circuit board: 8.46667cm x 5.64444cm
stripboards: 1

parts:
  Power_plug = Power plug
  R1 = Resistor [tolerance=±5% resistance=470 package=THT]
  IC1 = 74HCT245 [chip_label=74HCT245 package="DIP (Dual Inline) [THT]"]
  U1 = NodeMCU V3.0
  LED_Strip = Molex Picoblade Series Header [package=Picoblade-53398-0571]
  C1 = Electrolytic Capacitor [capacitance=1mF voltage=35V package="100 mil [THT, electrolytic]"]

nets (from the schematic view):
  GND: Power_plug.GND, IC1.pin10, IC1.pin19, U1.GND#6, U1.GND#13, U1.GND#16, U1.GND#33, LED_Strip.3, C1.-
  N1: Power_plug.VCC, LED_Strip.1, C1.+
  N2: R1.Pin_0, IC1.pin18
  N3: R1.Pin_1, LED_Strip.2
  N4: IC1.Direction, IC1.pin20, U1.Vin
  N5: IC1.A1, U1.D4

notes:
  homebridge-mculed - 5 Volt Strips, ESP8266/RGB/WS2811 LED Strip controller, 3.0
  LED Strip Connector
  1 - 5V - Red
  2 - DIN - Green
  3 - Gnd - White

custom parts:
  74HCT245: A DIP stand-in part for whatever IC you want. With 20 pins on a 300mil dual inline package (DIP) footprint.
  NodeMCU V3.0: ESP8266 based NodeMCU
