# Fritzing sketch mculed (saved by Fritzing 0.9.3b)
circuit board: 8.46667cm x 5.64444cm
breadboards: 3

parts:
  Part5 = Logic Level Converter
  Q1 = Basic FET N-Channel [part_number=FQP30N06L package="TO220 [THT]"]
  White_On/Off = Momentary Switch [package=ksa_sealed_tac_switch]
  LED_Strip = Header 5 [package=1x05-1mm-ra]
  M1 = RioRand LM2596
  Power_plug = Power plug
  Toggle_Color = Momentary Switch [package=ksa_sealed_tac_switch]
  U1 = NodeMCU V1.0
  part = Resistor [tolerance=±5% resistance=470 package=THT]
  C1 = Electrolytic Capacitor [capacitance=1mF voltage=35V package="100 mil [THT, electrolytic]"]

nets (from the schematic view):
  N1: Part5.RX2_LV, U1.D5
  GND: Part5.GND, Q1.source, White_On/Off.1, LED_Strip.5, M1.Pin_2, Power_plug.GND, Toggle_Color.1, U1.GND, C1.-
  N2: Part5.LV, U1.3V3
  N3: Part5.RX_LV, U1.D4
  N4: Part5.RX_HV, part.Pin_0
  N5: Part5.HV, M1.Pin_3, U1.Vin
  N6: Part5.RX2_HV, Q1.gate
  N7: Q1.drain, LED_Strip.4
  N8: White_On/Off.3, U1.D1
  N9: LED_Strip.1, M1.Pin_1, Power_plug.VCC, C1.+
  N10: Toggle_Color.3, U1.D2

notes:
  homebridge-mculed, ESP8266/RGB+W/WS2812 LED Strip controller, 1.0
  LED Strip Connector
  1 - 24V - Black
  2 - DIN - Red
  3 - Check - Green
  4 - W - Yellow
  5 - Gnd - Blue

custom parts:
  NodeMCU V1.0: ESP8266 based NodeMCU
