# Fritzing sketch ESP8266 - WSSensor (saved by Fritzing 0.9.3b)

parts:
  U1 = NodeMCU V1.0
  BME280 = GY-BMEP280 Barometric Pressure Sensor - Breakout
  PIR1 = PIR sensor

nets:
  N1: U1.D2, PIR1.SIG
  3V3: U1.3V3, BME280.VCC
  GND: U1.GND, BME280.GND, PIR1.GND
  N2: U1.D5, BME280.SCL
  N3: U1.D6, BME280.SDA
  VIN: U1.Vin, PIR1.VDD

notes:
  WSSensor
  BME-MS

custom parts:
  NodeMCU V1.0: ESP8266 based NodeMCU
  GY-BMEP280 Barometric Pressure Sensor - Breakout: The BME280 is a chip which was originally designed for the next generation of smartphones. It is made up of a very accurate pressure sensor and an associated temperature sensor which helps calibrate the pressure readings. And just for fun they threw in a pretty solid humidity sensor in there as well! So with an I2C connection you have access to enough weather data to make some pretty good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
