# Fritzing sketch mculed (saved by Fritzing 0.9.3b)
circuit board: 8.46667cm x 5.64444cm
breadboards: 3

parts:
  part = Logic Level Converter
  Q1 = Basic FET N-Channel [part_number=FQP30N06L package="TO220 [THT]"]
  White_On/Off = Momentary Switch [package=ksa_sealed_tac_switch]
  LED_Strip = Header 5 [package=1x05-1mm-ra]
  part_2 = RioRand LM2596
  Power_plug = Power plug
  Toggle_Color = Momentary Switch [package=ksa_sealed_tac_switch]
  part_3 = NodeMCU V1.0

nets (from the schematic view):
  N1: part.RX2_LV, part_3.D5
  GND: part.GND, Q1.source, White_On/Off.1, LED_Strip.5, part_2.Pin_2, Power_plug.GND, Toggle_Color.1, part_3.GND
  N2: part.LV, part_3.3V3
  N3: part.RX_LV, part_3.D4
  N4: part.RX_HV, LED_Strip.2
  N5: part.HV, part_2.Pin_3, part_3.Vin
  N6: part.RX2_HV, Q1.gate
  N7: Q1.drain, LED_Strip.4
  N8: White_On/Off.3, part_3.D1
  N9: LED_Strip.1, part_2.Pin_1, Power_plug.VCC
  N10: Toggle_Color.3, part_3.D2

notes:
  homebridge-mculed, ESP8266/RGB+W/WS2812 LED Strip controller, 1.0
  LED Strip Connector
  1 - 24V - Black
  2 - DIN - Red
  3 - Check - Green
  4 - W - Yellow
  5 - Gnd - Blue

custom parts:
  NodeMCU V1.0: ESP8266 based NodeMCU
