# Fritzing sketch mculed_v3_perf (saved by Fritzing 0.9.3b)
circuit board: 8.46667cm x 5.64444cm
stripboards: 2

parts:
  Q1 = Basic FET N-Channel [part_number=FQP30N06L package="TO220 [THT]"]
  M1 = RioRand LM2596
  Power_plug = Power plug
  R1 = Resistor [tolerance=±5% resistance=470 package=THT]
  IC1 = 74HCT245 [chip_label=74HCT245 package="DIP (Dual Inline) [THT]"]
  U1 = NodeMCU V3.0
  Toggle_Color = Round Pushbutton
  White_On/Off = Round Pushbutton
  LED_Strip = Molex Picoblade Series Header [package=Picoblade-53398-0571]
  C1 = Electrolytic Capacitor [capacitance=1mF voltage=35V package="100 mil [THT, electrolytic]"]

nets:
  N1: Q1.gate, IC1.pin17
  N2: Q1.drain, LED_Strip.4
  GND: Q1.source, M1.Pin_2, Power_plug.GND, IC1.pin10, IC1.pin19, U1.GND#6, U1.GND#13, U1.GND#16, U1.GND#33, Toggle_Color.leg1, White_On/Off.leg1, LED_Strip.5, C1.-
  N3: M1.Pin_1, Power_plug.VCC, LED_Strip.1, C1.+
  N4: M1.Pin_3, IC1.Direction, IC1.pin20, U1.Vin
  N5: R1.Pin_0, IC1.pin18
  N6: R1.Pin_1, LED_Strip.2
  N7: IC1.A1, U1.D4
  N8: IC1.pin3, U1.D5
  N9: U1.D1, White_On/Off.leg0
  N10: U1.D2, Toggle_Color.leg0

notes:
  homebridge-mculed, ESP8266/RGB+W/WS2812 LED Strip controller, 2.0
  LED Strip Connector
  1 - 24V - Black
  2 - DIN - Red
  3 - Check - Green
  4 - W - Yellow
  5 - Gnd - Blue

custom parts:
  74HCT245: A DIP stand-in part for whatever IC you want. With 20 pins on a 300mil dual inline package (DIP) footprint.
  NodeMCU V3.0: ESP8266 based NodeMCU
